// Logisim project ADD INSTRUCTION.circ as structural Verilog
module CPU_MEM_1 (
  input  in_1,
  input  in_2,
  output out_3
);

  wire nand_1_out, nand_2_out, nand_4_out;

  nand nand_1 (nand_1_out, in_1, in_2);
  nand nand_2 (nand_2_out, nand_1_out, in_2);
  nand nand_3 (out_3, nand_1_out, nand_4_out);
  nand nand_4 (nand_4_out, out_3, nand_2_out);
endmodule

module CPU_MEM_8 (
  input  [7:0] in_1,
  input  s,
  output [7:0] out_3
);

  CPU_MEM_1 cpu_mem_1_1 (.in_1(in_1[0]), .in_2(s), .out_3(out_3[0]));
  CPU_MEM_1 cpu_mem_1_2 (.in_1(in_1[1]), .in_2(s), .out_3(out_3[1]));
  CPU_MEM_1 cpu_mem_1_3 (.in_1(in_1[2]), .in_2(s), .out_3(out_3[2]));
  CPU_MEM_1 cpu_mem_1_4 (.in_1(in_1[3]), .in_2(s), .out_3(out_3[3]));
  CPU_MEM_1 cpu_mem_1_5 (.in_1(in_1[4]), .in_2(s), .out_3(out_3[4]));
  CPU_MEM_1 cpu_mem_1_6 (.in_1(in_1[5]), .in_2(s), .out_3(out_3[5]));
  CPU_MEM_1 cpu_mem_1_7 (.in_1(in_1[6]), .in_2(s), .out_3(out_3[6]));
  CPU_MEM_1 cpu_mem_1_8 (.in_1(in_1[7]), .in_2(s), .out_3(out_3[7]));
endmodule

module CPU_ENABLE_8 (
  input  [7:0] in_1,
  input  in_2,
  output [7:0] out_3
);

  wire and_1_out, and_2_out, and_3_out, and_4_out, and_5_out, and_6_out, and_7_out, and_8_out;

  assign out_3[0] = in_2 ? and_1_out : 1'bz;  // Controlled_Buffer controlled_buffer_1
  and and_1 (and_1_out, in_1[0], in_2);
  and and_2 (and_2_out, in_1[1], in_2);
  assign out_3[1] = in_2 ? and_2_out : 1'bz;  // Controlled_Buffer controlled_buffer_2
  and and_3 (and_3_out, in_1[2], in_2);
  assign out_3[2] = in_2 ? and_3_out : 1'bz;  // Controlled_Buffer controlled_buffer_3
  and and_4 (and_4_out, in_1[3], in_2);
  assign out_3[3] = in_2 ? and_4_out : 1'bz;  // Controlled_Buffer controlled_buffer_4
  and and_5 (and_5_out, in_1[4], in_2);
  assign out_3[4] = in_2 ? and_5_out : 1'bz;  // Controlled_Buffer controlled_buffer_5
  assign out_3[5] = in_2 ? and_6_out : 1'bz;  // Controlled_Buffer controlled_buffer_6
  and and_6 (and_6_out, in_1[5], in_2);
  assign out_3[6] = in_2 ? and_7_out : 1'bz;  // Controlled_Buffer controlled_buffer_7
  and and_7 (and_7_out, in_1[6], in_2);
  assign out_3[7] = in_2 ? and_8_out : 1'bz;  // Controlled_Buffer controlled_buffer_8
  and and_8 (and_8_out, in_1[7], in_2);
endmodule

module CPU_REGISTER_8 (
  input  [7:0] i,
  input  s,
  input  e,
  output [7:0] out_4,
  output [7:0] _0
);

  CPU_MEM_8 cpu_mem_8_1 (.s(s), .in_1(i), .out_3(out_4));
  CPU_ENABLE_8 cpu_enable_8_1 (.in_1(out_4), .out_3(_0), .in_2(e));
endmodule

module CPU_REG_BYTE (
  input  [7:0] i,
  input  h,
  input  v,
  input  s,
  input  e,
  output [7:0] o
);

  wire and_1_out, and_2_out, and_3_out;
  wire [7:0] cpu_register_8_1__0;

  and and_1 (and_1_out, h, v);
  and and_2 (and_2_out, and_1_out, s);
  and and_3 (and_3_out, and_1_out, e);
  CPU_REGISTER_8 cpu_register_8_1 (.i(i), .s(and_2_out), .e(and_3_out), ._0(cpu_register_8_1__0));  // open: out_4
  assign o = and_3_out ? cpu_register_8_1__0 : 8'bz;  // Controlled_Buffer controlled_buffer_1
endmodule

module CPU_NOT (
  input  [7:0] i,
  output [7:0] out_2
);

  not not_1 (out_2[0], i[0]);
  not not_2 (out_2[1], i[1]);
  not not_3 (out_2[2], i[2]);
  not not_4 (out_2[3], i[3]);
  not not_5 (out_2[4], i[4]);
  not not_6 (out_2[5], i[5]);
  not not_7 (out_2[6], i[6]);
  not not_8 (out_2[7], i[7]);
endmodule

module CPU_AND (
  input  [7:0] a,
  input  [7:0] b,
  output [7:0] o
);

  and and_1 (o[0], a[0], b[0]);
  and and_2 (o[1], a[1], b[1]);
  and and_3 (o[2], a[2], b[2]);
  and and_4 (o[3], a[3], b[3]);
  and and_5 (o[4], a[4], b[4]);
  and and_6 (o[5], a[5], b[5]);
  and and_7 (o[6], a[6], b[6]);
  and and_8 (o[7], a[7], b[7]);
endmodule

module CPU_OR (
  input  [7:0] a,
  input  [7:0] b,
  output [7:0] _0
);

  or or_1 (_0[0], a[0], b[0]);
  or or_2 (_0[1], a[1], b[1]);
  or or_3 (_0[2], a[2], b[2]);
  or or_4 (_0[3], a[3], b[3]);
  or or_5 (_0[4], a[4], b[4]);
  or or_6 (_0[5], a[5], b[5]);
  or or_7 (_0[6], a[6], b[6]);
  or or_8 (_0[7], a[7], b[7]);
endmodule

module CPU_XOR_1 (
  input  a,
  input  b,
  output o
);

  wire nand_1_out, nand_2_out, not_1_out, not_2_out;

  not not_1 (not_1_out, a);
  not not_2 (not_2_out, b);
  nand nand_1 (nand_1_out, not_1_out, b);
  nand nand_2 (nand_2_out, a, not_2_out);
  nand nand_3 (o, nand_1_out, nand_2_out);
endmodule

module CPU_SHR (
  input  [7:0] i,
  input  shift_in,
  output shift_out,
  output [7:0] o
);

  wire [7:1] cpu_register_8_1__0;

  CPU_REGISTER_8 cpu_register_8_1 (.i(i), .s(1'b1), .e(1'b1), ._0({cpu_register_8_1__0, shift_out}));  // open: out_4
  CPU_REGISTER_8 cpu_register_8_2 (.i({shift_in, cpu_register_8_1__0}), .s(1'b1), .e(1'b1), ._0(o));  // open: out_4
endmodule

module CPU_SHL (
  input  shift_in,
  input  [7:0] i,
  output [7:0] o,
  output shift_out
);

  wire [6:0] cpu_register_8_1__0;

  CPU_REGISTER_8 cpu_register_8_1 (.i(i), .s(1'b1), .e(1'b1), ._0({shift_out, cpu_register_8_1__0}));  // open: out_4
  CPU_REGISTER_8 cpu_register_8_2 (.i({cpu_register_8_1__0, shift_in}), .s(1'b1), .e(1'b1), ._0(o));  // open: out_4
endmodule

module CPU_ADDER (
  input  a,
  input  b,
  input  carry_in,
  output sum,
  output carry_out
);

  wire and_1_out, and_2_out, cpu_xor_1_1_o;

  CPU_XOR_1 cpu_xor_1_1 (.a(a), .b(b), .o(cpu_xor_1_1_o));
  and and_1 (and_1_out, carry_in, cpu_xor_1_1_o);
  and and_2 (and_2_out, a, b);
  CPU_XOR_1 cpu_xor_1_2 (.a(cpu_xor_1_1_o), .b(carry_in), .o(sum));
  or or_1 (carry_out, and_1_out, and_2_out);
endmodule

module CPU_ADDER_8 (
  input  [7:0] a,
  input  [7:0] b,
  input  carry_in,
  output carry_out,
  output [7:0] out_5
);

  wire cpu_adder_2_carry_out, cpu_adder_3_carry_out, cpu_adder_4_carry_out, cpu_adder_5_carry_out,
       cpu_adder_6_carry_out, cpu_adder_7_carry_out, cpu_adder_8_carry_out;

  CPU_ADDER cpu_adder_1 (.a(a[7]), .b(b[7]), .carry_in(cpu_adder_2_carry_out), .sum(out_5[7]), .carry_out(carry_out));
  CPU_ADDER cpu_adder_2 (
    .a(a[6]), .b(b[6]), .carry_in(cpu_adder_3_carry_out), .sum(out_5[6]), .carry_out(cpu_adder_2_carry_out));
  CPU_ADDER cpu_adder_3 (
    .a(a[5]), .b(b[5]), .carry_in(cpu_adder_4_carry_out), .sum(out_5[5]), .carry_out(cpu_adder_3_carry_out));
  CPU_ADDER cpu_adder_4 (
    .a(a[4]), .b(b[4]), .carry_in(cpu_adder_5_carry_out), .sum(out_5[4]), .carry_out(cpu_adder_4_carry_out));
  CPU_ADDER cpu_adder_5 (
    .a(a[3]), .b(b[3]), .carry_in(cpu_adder_6_carry_out), .sum(out_5[3]), .carry_out(cpu_adder_5_carry_out));
  CPU_ADDER cpu_adder_6 (
    .a(a[2]), .b(b[2]), .carry_in(cpu_adder_7_carry_out), .sum(out_5[2]), .carry_out(cpu_adder_6_carry_out));
  CPU_ADDER cpu_adder_7 (
    .a(a[1]), .b(b[1]), .carry_in(cpu_adder_8_carry_out), .sum(out_5[1]), .carry_out(cpu_adder_7_carry_out));
  CPU_ADDER cpu_adder_8 (.a(a[0]), .b(b[0]), .carry_in(carry_in), .sum(out_5[0]), .carry_out(cpu_adder_8_carry_out));
endmodule

module CPU_XOR_LE_1 (
  input  above_equal,
  input  a_larger,
  input  a,
  input  b,
  output c,
  output equal,
  output a_large
);

  wire and_2_out, not_1_out;

  CPU_XOR_1 cpu_xor_1_1 (.a(a), .b(b), .o(c));
  not not_1 (not_1_out, c);
  and and_1 (equal, not_1_out, above_equal);
  and and_2 (and_2_out, above_equal, a, c);
  or or_1 (a_large, and_2_out, a_larger);
endmodule

module CPU_XOR_LE_8 (
  input  [7:0] a,
  input  [7:0] b,
  output [7:0] out_3,
  output larger,
  output equal
);

  wire cpu_xor_le_1_1_a_large, cpu_xor_le_1_1_equal, cpu_xor_le_1_2_a_large, cpu_xor_le_1_2_equal,
       cpu_xor_le_1_3_a_large, cpu_xor_le_1_3_equal, cpu_xor_le_1_4_a_large, cpu_xor_le_1_4_equal,
       cpu_xor_le_1_5_a_large, cpu_xor_le_1_5_equal, cpu_xor_le_1_6_a_large, cpu_xor_le_1_6_equal,
       cpu_xor_le_1_7_a_large, cpu_xor_le_1_7_equal;

  CPU_XOR_LE_1 cpu_xor_le_1_1 (
    .a(a[0]), .b(b[0]), .a_larger(1'b0), .c(out_3[0]), .above_equal(1'b1), .equal(cpu_xor_le_1_1_equal),
    .a_large(cpu_xor_le_1_1_a_large));
  CPU_XOR_LE_1 cpu_xor_le_1_2 (
    .a(a[1]), .b(b[1]), .a_larger(cpu_xor_le_1_1_a_large), .c(out_3[1]), .above_equal(cpu_xor_le_1_1_equal),
    .equal(cpu_xor_le_1_2_equal), .a_large(cpu_xor_le_1_2_a_large));
  CPU_XOR_LE_1 cpu_xor_le_1_3 (
    .a(a[2]), .b(b[2]), .a_larger(cpu_xor_le_1_2_a_large), .c(out_3[2]), .above_equal(cpu_xor_le_1_2_equal),
    .equal(cpu_xor_le_1_3_equal), .a_large(cpu_xor_le_1_3_a_large));
  CPU_XOR_LE_1 cpu_xor_le_1_4 (
    .a(a[3]), .b(b[3]), .a_larger(cpu_xor_le_1_3_a_large), .c(out_3[3]), .above_equal(cpu_xor_le_1_3_equal),
    .equal(cpu_xor_le_1_4_equal), .a_large(cpu_xor_le_1_4_a_large));
  CPU_XOR_LE_1 cpu_xor_le_1_5 (
    .a(a[4]), .b(b[4]), .a_larger(cpu_xor_le_1_4_a_large), .c(out_3[4]), .above_equal(cpu_xor_le_1_4_equal),
    .equal(cpu_xor_le_1_5_equal), .a_large(cpu_xor_le_1_5_a_large));
  CPU_XOR_LE_1 cpu_xor_le_1_6 (
    .a(a[5]), .b(b[5]), .a_larger(cpu_xor_le_1_5_a_large), .c(out_3[5]), .above_equal(cpu_xor_le_1_5_equal),
    .equal(cpu_xor_le_1_6_equal), .a_large(cpu_xor_le_1_6_a_large));
  CPU_XOR_LE_1 cpu_xor_le_1_7 (
    .a(a[6]), .b(b[6]), .a_larger(cpu_xor_le_1_6_a_large), .c(out_3[6]), .above_equal(cpu_xor_le_1_6_equal),
    .equal(cpu_xor_le_1_7_equal), .a_large(cpu_xor_le_1_7_a_large));
  CPU_XOR_LE_1 cpu_xor_le_1_8 (
    .a(a[7]), .b(b[7]), .a_larger(cpu_xor_le_1_7_a_large), .c(out_3[7]), .above_equal(cpu_xor_le_1_7_equal),
    .equal(equal), .a_large(larger));
endmodule

module CPU_Z (
  input  [7:0] i,
  output o
);

  wire or_1_out;

  or or_1 (or_1_out, i[0], i[1], i[2], i[3], i[4], i[5], i[6], i[7]);
  not not_1 (o, or_1_out);
endmodule

module CPU_DECODER_3x8 (
  input  a,
  input  b,
  input  c,
  output [7:0] o
);

  wire not_1_out, not_2_out, not_3_out;

  not not_1 (not_1_out, c);
  not not_2 (not_2_out, b);
  not not_3 (not_3_out, a);
  and and_1 (o[0], not_3_out, not_2_out, not_1_out);
  and and_2 (o[1], not_3_out, not_2_out, c);
  and and_3 (o[2], not_3_out, b, not_1_out);
  and and_4 (o[3], not_3_out, b, c);
  and and_5 (o[4], a, not_2_out, not_1_out);
  and and_6 (o[5], a, not_2_out, c);
  and and_7 (o[6], a, b, not_1_out);
  and and_8 (o[7], a, b, c);
endmodule

module CPU_E (
  input  [7:0] in_1,
  input  in_2,
  output [7:0] out_3
);

  wire and_1_out, and_2_out, and_3_out, and_4_out, and_5_out, and_6_out, and_7_out, and_8_out;

  assign out_3[0] = in_2 ? and_1_out : 1'bz;  // Controlled_Buffer controlled_buffer_1
  and and_1 (and_1_out, in_1[0], in_2);
  assign out_3[1] = in_2 ? and_2_out : 1'bz;  // Controlled_Buffer controlled_buffer_2
  and and_2 (and_2_out, in_1[1], in_2);
  assign out_3[2] = in_2 ? and_3_out : 1'bz;  // Controlled_Buffer controlled_buffer_3
  and and_3 (and_3_out, in_1[2], in_2);
  and and_4 (and_4_out, in_1[3], in_2);
  assign out_3[3] = in_2 ? and_4_out : 1'bz;  // Controlled_Buffer controlled_buffer_4
  and and_5 (and_5_out, in_1[4], in_2);
  assign out_3[4] = in_2 ? and_5_out : 1'bz;  // Controlled_Buffer controlled_buffer_5
  and and_6 (and_6_out, in_1[5], in_2);
  assign out_3[5] = in_2 ? and_6_out : 1'bz;  // Controlled_Buffer controlled_buffer_6
  and and_7 (and_7_out, in_1[6], in_2);
  assign out_3[6] = in_2 ? and_7_out : 1'bz;  // Controlled_Buffer controlled_buffer_7
  assign out_3[7] = in_2 ? and_8_out : 1'bz;  // Controlled_Buffer controlled_buffer_8
  and and_8 (and_8_out, in_1[7], in_2);
endmodule

module CPU_ALU (
  input  [7:0] a,
  input  [7:0] b,
  input  carry_in,
  input  a_2,
  input  b_2,
  input  c,
  output a_larger,
  output equal,
  output zero,
  output [7:0] c_2,
  output carry_out
);

  wire and_1_out, and_2_out, and_3_out, cpu_adder_8_1_carry_out, cpu_shl_1_shift_out, cpu_shr_1_shift_out;
  wire [7:0] cpu_adder_8_1_out_5, cpu_and_1_o, cpu_decoder_3x8_1_o, cpu_not_1_out_2, cpu_or_1__0,
       cpu_shl_1_o, cpu_shr_1_o, cpu_xor_le_8_1_out_3;

  CPU_XOR_LE_8 cpu_xor_le_8_1 (.a(a), .b(b), .out_3(cpu_xor_le_8_1_out_3), .larger(a_larger), .equal(equal));
  CPU_AND cpu_and_1 (.a(a), .o(cpu_and_1_o), .b(b));
  CPU_NOT cpu_not_1 (.i(a), .out_2(cpu_not_1_out_2));
  CPU_SHL cpu_shl_1 (.shift_in(carry_in), .i(a), .o(cpu_shl_1_o), .shift_out(cpu_shl_1_shift_out));
  CPU_SHR cpu_shr_1 (.shift_out(cpu_shr_1_shift_out), .i(a), .o(cpu_shr_1_o), .shift_in(carry_in));
  CPU_ADDER_8 cpu_adder_8_1 (
    .a(a), .b(b), .carry_out(cpu_adder_8_1_carry_out), .out_5(cpu_adder_8_1_out_5), .carry_in(carry_in));
  CPU_OR cpu_or_1 (.a(a), .b(b), ._0(cpu_or_1__0));
  CPU_DECODER_3x8 cpu_decoder_3x8_1 (.a(a_2), .b(b_2), .c(c), .o(cpu_decoder_3x8_1_o));
  CPU_E cpu_e_1 (.in_1(cpu_xor_le_8_1_out_3), .out_3(c_2), .in_2(cpu_decoder_3x8_1_o[6]));
  CPU_E cpu_e_2 (.in_1(cpu_or_1__0), .out_3(c_2), .in_2(cpu_decoder_3x8_1_o[5]));
  CPU_E cpu_e_3 (.in_1(cpu_and_1_o), .out_3(c_2), .in_2(cpu_decoder_3x8_1_o[4]));
  CPU_E cpu_e_4 (.in_1(cpu_not_1_out_2), .out_3(c_2), .in_2(cpu_decoder_3x8_1_o[3]));
  CPU_E cpu_e_5 (.in_1(cpu_shl_1_o), .out_3(c_2), .in_2(cpu_decoder_3x8_1_o[2]));
  CPU_E cpu_e_6 (.in_1(cpu_shr_1_o), .out_3(c_2), .in_2(cpu_decoder_3x8_1_o[1]));
  CPU_E cpu_e_7 (.in_1(cpu_adder_8_1_out_5), .out_3(c_2), .in_2(cpu_decoder_3x8_1_o[0]));
  and and_1 (and_1_out, cpu_shl_1_shift_out, cpu_decoder_3x8_1_o[2]);
  assign carry_out = cpu_decoder_3x8_1_o[2] ? and_1_out : 1'bz;  // Controlled_Buffer controlled_buffer_1
  assign carry_out = cpu_decoder_3x8_1_o[1] ? and_2_out : 1'bz;  // Controlled_Buffer controlled_buffer_2
  and and_2 (and_2_out, cpu_shr_1_shift_out, cpu_decoder_3x8_1_o[1]);
  and and_3 (and_3_out, cpu_adder_8_1_carry_out, cpu_decoder_3x8_1_o[0]);
  assign carry_out = cpu_decoder_3x8_1_o[0] ? and_3_out : 1'bz;  // Controlled_Buffer controlled_buffer_3
  CPU_Z cpu_z_1 (.i(c_2), .o(zero));
endmodule

module CPU_BUS_1 (
  input  [7:0] i,
  input  bus_1,
  output [7:0] o
);

  wire not_1_out;

  and and_1 (o[7], i[7], not_1_out);
  and and_2 (o[6], i[6], not_1_out);
  and and_3 (o[5], i[5], not_1_out);
  and and_4 (o[4], i[4], not_1_out);
  and and_5 (o[3], i[3], not_1_out);
  and and_6 (o[2], i[2], not_1_out);
  and and_7 (o[1], i[1], not_1_out);
  not not_1 (not_1_out, bus_1);
  or or_1 (o[0], i[0], bus_1);
endmodule

module CPU_ACCUMULATOR (
  input  [7:0] i,
  input  s,
  input  e,
  output [7:0] o
);

  CPU_REGISTER_8 cpu_register_8_1 (.i(i), .s(s), .e(e), ._0(o));  // open: out_4
endmodule

module CPU_R (
  input  [7:0] i,
  input  s,
  input  e,
  output [7:0] out_4,
  output [7:0] o
);

  CPU_REGISTER_8 cpu_register_8_1 (.i(i), .s(s), .e(e), ._0(o), .out_4(out_4));
endmodule

module CPU_TMP (
  input  [7:0] i,
  input  s,
  output [7:0] o
);

  wire [7:0] controlled_buffer_1_out;

  assign controlled_buffer_1_out = s ? i : 8'bz;  // Controlled_Buffer controlled_buffer_1
  CPU_MEM_8 cpu_mem_8_1 (.s(s), .in_1(controlled_buffer_1_out), .out_3(o));
endmodule

module CPU_STEPPER (
  input  reset,
  input  clk,
  output step_1,
  output step_2,
  output step_3,
  output step_4
);

  wire cpu_mem_1_1_out_3, cpu_mem_1_2_out_3, cpu_mem_1_3_out_3, cpu_mem_1_4_out_3, cpu_mem_1_5_out_3,
       not_1_out, not_2_out, not_3_out, not_4_out, not_5_out, or_1_out, or_2_out;

  not not_1 (not_1_out, clk);
  not not_2 (not_2_out, reset);
  or or_1 (or_1_out, reset, clk);
  or or_2 (or_2_out, reset, not_1_out);
  or or_3 (step_1, reset, not_3_out);
  CPU_MEM_1 cpu_mem_1_1 (.in_1(not_2_out), .in_2(or_1_out), .out_3(cpu_mem_1_1_out_3));
  not not_3 (not_3_out, cpu_mem_1_2_out_3);
  CPU_MEM_1 cpu_mem_1_2 (.in_1(cpu_mem_1_1_out_3), .in_2(or_2_out), .out_3(cpu_mem_1_2_out_3));
  and and_1 (step_2, cpu_mem_1_2_out_3, not_4_out);
  not not_4 (not_4_out, cpu_mem_1_4_out_3);
  CPU_MEM_1 cpu_mem_1_3 (.in_1(cpu_mem_1_2_out_3), .in_2(or_1_out), .out_3(cpu_mem_1_3_out_3));
  CPU_MEM_1 cpu_mem_1_4 (.in_1(cpu_mem_1_3_out_3), .in_2(or_2_out), .out_3(cpu_mem_1_4_out_3));
  and and_2 (step_3, cpu_mem_1_4_out_3, not_5_out);
  CPU_MEM_1 cpu_mem_1_5 (.in_1(cpu_mem_1_4_out_3), .in_2(or_1_out), .out_3(cpu_mem_1_5_out_3));
  not not_5 (not_5_out, step_4);
  CPU_MEM_1 cpu_mem_1_6 (.in_1(cpu_mem_1_5_out_3), .in_2(or_2_out), .out_3(step_4));

  // Notes on the sheet:
  //   reset: pull=up
endmodule

module CPU (
  input  [7:0] s,
  input  [7:0] s_2,
  input  s_3,
  input  s_4,
  input  s_5,
  output [7:0] out_6,
  output C_OUT,
  output a___b,
  output a___b_2,
  output ZERO
);

  wire clock_1_out, cpu_clk_1_clk, cpu_clk_1_clke, cpu_clk_1_clks, cpu_control_section_1_acc_e,
       cpu_control_section_1_acc_s, cpu_control_section_1_r0_e, cpu_control_section_1_r1_e,
       cpu_control_section_1_r2_e, cpu_control_section_1_r2_s, cpu_control_section_1_r3_e,
       cpu_control_section_1_r3_s, cpu_control_section_1_tmp_s;
  wire [7:0] cpu_accumulator_1_o, cpu_alu_1_c_2, cpu_tmp_1_o;

  CPU_ACCUMULATOR cpu_accumulator_1 (
    .i(cpu_alu_1_c_2), .o(cpu_accumulator_1_o), .s(cpu_control_section_1_acc_s),
    .e(cpu_control_section_1_acc_e));
  CPU_TMP cpu_tmp_1 (.i(cpu_accumulator_1_o), .o(cpu_tmp_1_o), .s(cpu_control_section_1_tmp_s));
  CPU_ALU cpu_alu_1 (
    .a(cpu_accumulator_1_o), .b(cpu_tmp_1_o), .carry_in(1'b0), .a_2(s_3), .b_2(s_4), .c(s_5), .zero(ZERO),
    .c_2(cpu_alu_1_c_2), .carry_out(C_OUT), .a_larger(a___b), .equal(a___b_2));
  Clock clock_1 (.out(clock_1_out));
  CPU_CLK cpu_clk_1 (.clk(cpu_clk_1_clk), .clks(cpu_clk_1_clks), .clkin(clock_1_out), .clke(cpu_clk_1_clke));
  CPU_CONTROL_SECTION cpu_control_section_1 (
    .clks(cpu_clk_1_clks), .clke(cpu_clk_1_clke), .clk(cpu_clk_1_clk), .ACC_S(cpu_control_section_1_acc_s),
    .TMP_S(cpu_control_section_1_tmp_s), .R2_S(cpu_control_section_1_r2_s),
    .R3_S(cpu_control_section_1_r3_s), .ACC_E(cpu_control_section_1_acc_e),
    .R0_E(cpu_control_section_1_r0_e), .R1_E(cpu_control_section_1_r1_e), .R2_E(cpu_control_section_1_r2_e),
    .R3_E(cpu_control_section_1_r3_e));  // open: RO_S, R1_S
  CPU_R cpu_r_1 (.i(s), .o(cpu_accumulator_1_o), .s(1'b1), .e(cpu_control_section_1_r0_e));  // open: out_4
  CPU_R cpu_r_2 (.i(s_2), .o(cpu_accumulator_1_o), .s(1'b1), .e(cpu_control_section_1_r1_e));  // open: out_4
  CPU_R cpu_r_3 (
    .i(cpu_accumulator_1_o), .o(cpu_accumulator_1_o), .s(cpu_control_section_1_r2_s),
    .e(cpu_control_section_1_r2_e));  // open: out_4
  CPU_R cpu_r_4 (
    .i(cpu_accumulator_1_o), .s(cpu_control_section_1_r3_s), .e(cpu_control_section_1_r3_e), .out_4(out_6));  // open: o
endmodule

module CPU_CONTROL_SECTION (
  input  clks,
  input  clk,
  input  clke,
  output ACC_E,
  output ACC_S,
  output TMP_S,
  output R0_E,
  output RO_S,
  output R1_E,
  output R1_S,
  output R2_E,
  output R2_S,
  output R3_E,
  output R3_S
);

  wire cpu_stepper_1_step_1, cpu_stepper_1_step_2, cpu_stepper_1_step_3, cpu_stepper_1_step_4;

  and and_1 (ACC_E, clke, cpu_stepper_1_step_3);
  and and_2 (R0_E, clke, cpu_stepper_1_step_2);
  and and_3 (R1_E, clke, cpu_stepper_1_step_1);
  and and_4 (R2_E, clke, 1'b0);
  and and_5 (R3_E, clke, 1'b0);
  CPU_STEPPER cpu_stepper_1 (
    .clk(clk), .step_1(cpu_stepper_1_step_1), .step_2(cpu_stepper_1_step_2), .step_3(cpu_stepper_1_step_3),
    .step_4(cpu_stepper_1_step_4), .reset(cpu_stepper_1_step_4));
  and and_6 (ACC_S, clks, cpu_stepper_1_step_2);
  and and_7 (TMP_S, clks, cpu_stepper_1_step_1);
  and and_8 (RO_S, clks, 1'b0);
  and and_9 (R1_S, clks, 1'b0);
  and and_10 (R2_S, clks, 1'b0);
  and and_11 (R3_S, clks, cpu_stepper_1_step_3);
endmodule

module CPU_CLK (
  input  clkin,
  output clk,
  output clks,
  output clke
);

  wire j_k_ff_1_qn, nand_1_out;

  J_K_Flip_Flop j_k_ff_1 (.J(1'b1), .clk(clkin), .K(1'b1), .Q(clk), .Qn(j_k_ff_1_qn));  // open: preset, en, reset
  nand nand_1 (nand_1_out, clkin, clk);
  nand nand_2 (clke, j_k_ff_1_qn, clkin);
  not not_1 (clks, nand_1_out);

  // Notes on the sheet:
  //   clkin: pull=down
  //   clk: pull=down
  //   clks: pull=down
  //   clke: pull=down
endmodule
